# Fritzing sketch AFPSDLSMS (saved by Fritzing 0.9.3b)

parts:
  Part1 = Arduino Uno (Rev3)
  LCD1 = LCD screen
  LCM1602_IIC3 = LCM1602 IIC [part_number="LCM1602 IIC" chip_label="LCM1602 IIC" package="DIP (Dual Inline) [THT]"]
  GSM_SIM_GPSR_SMS_SIM900_SIM1 = SIM800L [package=THT]
  R1 = Resistor [tolerance=±5% resistance=1k package=THT]
  Q1 = NPN-Transistor [package="TO92 [THT]"]
  R3 = Resistor [tolerance=±5% resistance=10k package=THT]
  R4 = Resistor [tolerance=±5% resistance=22k package=THT]
  Part2 = sensor_biometrico
  KY-1 = Keyes Relay [package=THT]
  L1 = Solenoid
  Power_plug1 = Power plug

nets:
  N1: Part1.A4/SDA, LCM1602_IIC3.SDA
  N2: Part1.A5/SCL, LCM1602_IIC3.SCL
  N3: Part1.D10_PWM/SS, GSM_SIM_GPSR_SMS_SIM900_SIM1.SIM_TXD
  N4: Part1.D11_PWM/MOSI, R3.Pin_1
  GND: Part1.GND, LCM1602_IIC3.GND, GSM_SIM_GPSR_SMS_SIM900_SIM1.GND, Q1.E, R4.Pin_0, Part2.GND, KY-1.ground
  N5: Part1.D0/RX, Part2.RX
  N6: Part1.D1/TX, Part2.TX
  N7: Part1.D2, R1.Pin_1
  N8: Part1.D3_PWM, KY-1.signal
  5V: Part1.5V, LCM1602_IIC3.VCC, GSM_SIM_GPSR_SMS_SIM900_SIM1.5V, Part2.VCC, KY-1.power
  VSS: LCD1.VSS, LCM1602_IIC3.VSS
  VDD: LCD1.VDD, LCM1602_IIC3.VDD
  N9: LCD1.V0, LCM1602_IIC3.V0
  N10: LCD1.RS, LCM1602_IIC3.RS
  N11: LCD1.R/W, LCM1602_IIC3.RW
  N12: LCD1.E, LCM1602_IIC3.E
  N13: LCD1.DB0, LCM1602_IIC3.D0
  N14: LCD1.DB1, LCM1602_IIC3.D1
  N15: LCD1.DB2, LCM1602_IIC3.D2
  N16: LCD1.DB3, LCM1602_IIC3.D3
  N17: LCD1.DB4, LCM1602_IIC3.D4
  N18: LCD1.DB5, LCM1602_IIC3.D5
  N19: LCD1.DB6, LCM1602_IIC3.D6
  N20: LCD1.DB7, LCM1602_IIC3.D7
  N21: LCD1.LED+, LCM1602_IIC3.A
  N22: LCD1.LED-, LCM1602_IIC3.K
  N23: GSM_SIM_GPSR_SMS_SIM900_SIM1.SIM_RXD, R3.Pin_0, R4.Pin_1
  N24: GSM_SIM_GPSR_SMS_SIM900_SIM1.RST, Q1.C
  N25: R1.Pin_0, Q1.B
  N26: KY-1.C, Power_plug1.VCC
  N27: KY-1.NO, L1.pin2
  N28: L1.pin1, Power_plug1.GND

custom parts:
  LCM1602 IIC: I2C-Module to use a 1602 or 2004 LCD on with the wire.h libory Serial LCD Modul
  sensor_biometrico: Adafruit Optical Fingerprint Sensor
  Keyes Relay: The Keyes 5V relay module is suitable for SCM development, home appliance control. It uses a 5V~12V TIL control signal which can control DC / AC signal.
